# Fritzing sketch ravenhid (saved by Fritzing 0.8.3b)
circuit board: 6cm x 4cm
breadboards: 1

parts:
  Vcc_Ctr_Pos = Power plug
  +5Vreg = Voltage Regulator - 5V [package="TO220 [THT]"]
  Reset = Pushbutton [package="[THT]"]
  R2 = Resistor [tolerance=±5% resistance=1M package=THT]
  +5V_GND_Vcc = male pin header, 3 pins [form="♂ (male)"]
  D2 = Rectifier Diode [part_number=1N4004 package="300 mil [THT]"]
  C6 = Ceramic Capacitor [capacitance=0.1µF voltage=50V package="100 mil [THT, multilayer]"]
  C7 = Ceramic Capacitor [capacitance=100pF voltage=50V package="100 mil [THT, multilayer]"]
  C5 = Ceramic Capacitor [capacitance=0.1µF voltage=50V package="100 mil [THT, multilayer]"]
  R3 = Resistor [tolerance=±5% resistance=10k package=THT]
  C1 = Ceramic Capacitor [capacitance=10µF package="100 mil [THT, multilayer]"]
  FTDI = male pin header, 6 pins [form="♂ (male)"]
  C8 = Electrolytic Capacitor [capacitance=47µF voltage=50V package="100 mil [THT, electrolytic]"]
  16MHz = Resonator [frequency="16 Mhz" package=THT]
  RFID = screw terminal, 4 pins
  BLEMini = female pin header, 4 pins [form="♀ (female)"]
  MicroSD = MicroSD Breakout
  R4 = Resistor [tolerance=±5% resistance=10k package=THT]
  Atmega328p = atmega168 [package="DIP28 [THT]"]
  LCD = Adafruit Negative RGB 2x16 LCD
  Contrast = TRIMPOT [package=trim_pot_pth]

nets:
  GND: Vcc_Ctr_Pos.GND, +5Vreg.GND, Reset.Pin_3, Reset.Pin_4, +5V_GND_Vcc.pin2, C6.0, C7.0, C1.1, FTDI.pin1, C8.-, 16MHz.GND, RFID.pin1, BLEMini.pin2, MicroSD.GND, Atmega328p.Pin_8, Atmega328p.Pin_22, LCD.no_name_yet#0, LCD.no_name_yet#4, Contrast.CCW
  N1: Vcc_Ctr_Pos.VCC, D2.anode
  12V: +5Vreg.input_voltage, +5V_GND_Vcc.pin3, D2.cathode, C6.1, C7.1, C8.+, RFID.pin4
  5V: +5Vreg.output_voltage, +5V_GND_Vcc.pin1, R3.Pin_0, C1.0, FTDI.pin3, BLEMini.pin1, MicroSD.5V, R4.Pin_1, Atmega328p.Pin_7, Atmega328p.Pin_20, LCD.no_name_yet#1, LCD.no_name_yet#14, Contrast.CW
  N2: Reset.Pin_1, Reset.Pin_2, C5.1, Atmega328p.Pin_1
  N3: R2.Pin_0, 16MHz.0, Atmega328p.Pin_9
  N4: R2.Pin_1, 16MHz.pin_1, Atmega328p.Pin_10
  N5: C5.0, R3.Pin_1, FTDI.pin6
  N6: FTDI.pin4, BLEMini.pin3, Atmega328p.Pin_2
  N7: FTDI.pin5, BLEMini.pin4, Atmega328p.Pin_3
  N8: RFID.pin2, Atmega328p.Pin_5
  N9: RFID.pin3, Atmega328p.Pin_6
  N10: MicroSD.CD, R4.Pin_0, Atmega328p.Pin_15
  N11: MicroSD.CS, Atmega328p.Pin_16
  N12: MicroSD.DI, Atmega328p.Pin_17
  N13: MicroSD.DO, Atmega328p.Pin_18
  N14: MicroSD.CLK, Atmega328p.Pin_19
  N15: Atmega328p.Pin_11, LCD.no_name_yet#13
  N16: Atmega328p.Pin_12, LCD.no_name_yet#12
  N17: Atmega328p.Pin_13, LCD.no_name_yet#11
  N18: Atmega328p.Pin_14, LCD.no_name_yet#10
  N19: Atmega328p.Pin_23, LCD.no_name_yet#3
  N20: Atmega328p.Pin_24, LCD.no_name_yet#5
  N21: Atmega328p.Pin_25, LCD.no_name_yet#15
  N22: Atmega328p.Pin_26, LCD.no_name_yet#16
  N23: Atmega328p.Pin_27, LCD.no_name_yet#17
  N24: LCD.no_name_yet#2, Contrast.WIPER

notes:
  RavenHID
  D7
  VIN
  GND
  TX
  RX
  D0
  D1
  12v
  https://github.com/emperorcow/ravenhid
  Designed By:
  Lucas Morris
  Adam Zamora
  v1.0

custom parts:
  MicroSD Breakout: 5V-ready microSD Breakout with Level Shifter
  Adafruit Negative RGB 2x16 LCD: Adafruit Negative 2x16 LCD Display with RGB Backlight
